# Fritzing sketch ThermostatWiringDiagram (saved by Fritzing 0.9.10b)

parts:
  part = Raspberry Pi Pico
  part_2 = KY-015 Temperature & Humidity Sensor Module [package="Breakout board"]
  part_3 = LCD1602-I2C

nets:
  N1: part.pin_3, part.pin_33, part.pin_38, part.pin_42, part_2.-, part_3.GND
  N2: part.pin_6, part_3.SDA
  N3: part.pin_7, part_3.SCL
  N4: part.pin_34, part_2.S
  VIN: part.pin_40, part_2.Vin, part_3.VCC

custom parts:
  Raspberry Pi Pico: Raspberry Pi Pico. Based around the RP2040 microcontroller the Pico is a low cost microcontroller device bringing Raspberry Pi quality, cost, and easy of use to the microcontroller space. Jan 2021, Split part in to two versions: tht (this one) and SMD. This one will drill holes for a .1 in header in pcb to allow plugging in the module as well as providing pads to solder the module to the top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
  KY-015 Temperature & Humidity Sensor Module: KY-015 temperature and humidity sensor module, provides a low-latency serial interface to measure humidity and temperature.
  LCD1602-I2C: A standard character display, usually with 2x16 characters. Comes in many colors with LCM1602 IIC attached.
